# Fritzing sketch schema (saved by Fritzing 0.9.2b)

parts:
  GY1 = MPU-6050 Board GY-521 [form="♀ (female)" package=THT]
  Part1 = Arduino Uno (Rev3)
  Part2 = Intel Galileo  # not connected

nets:
  N1: GY1.pin1, Part1.3V3
  N2: GY1.pin2, Part1.GND
  N3: GY1.pin3, Part1.A5/SCL
  N4: GY1.pin4, Part1.A4/SDA
  N5: GY1.pin8, Part1.D2

custom parts:
  MPU-6050 Board GY-521: Acelerometro y Giroscopio MPU-6050 Board GY-521
